// Logisim project stazione.circ as structural Verilog: 10 circuits, main circuit main
module main (
  input  POWER
);

  wire button_2_out, button_out, ckl, comparator_1_gt, d_ff_1_q, decoder_1_out0, next_1_out_8, ON, or_1_out;
  wire [1:0] next_1_out_6;
  wire [3:0] min0, min1, next_1_out_7, timer_1_out_5, timer_1_out_6, timer_1_out_7, timer_1_out_8;
  wire [5:0] counter_1_q, orario_1_out_3;
  wire [6:0] lettera_a_i_i_1_out_3, lettera_a_i_i_1_out_4, lettera_a_i_i_1_output, lettera_i_a_o_1_out_3,
       lettera_i_a_o_1_out_4, lettera_i_a_o_1_output, lettera_l_v_d_1_out_3, lettera_l_v_d_1_out_4,
       lettera_l_v_d_1_output, lettera_m_p_l_1_out_3, lettera_m_p_l_1_out_4, lettera_m_p_l_1_output,
       lettera_n_a_1_out_3, lettera_n_a_1_out_4, lettera_n_a_1_output, lettera_o_1_out_3, lettera_o_1_out_4,
       lettera_o_1_output;

  Clock clock_1 (.out(ckl));
  Decoder decoder_1 (.out0(decoder_1_out0), .out1(ON), .sel(d_ff_1_q));  // open: en
  D_Flip_Flop d_ff_1 (.clk(ckl), .D(POWER), .Q(d_ff_1_q));  // open: Qn, preset, en, reset
  LED led_1 (.in(decoder_1_out0));
  LED led_2 (.in(decoder_1_out0));
  LED led_3 (.in(decoder_1_out0));
  LED led_4 (.in(decoder_1_out0));
  Button button (.out(button_out));
  Button button_2 (.out(button_2_out));
  Counter #(.width(6), .max('h5), .ongoal("stay")) counter_1 (
    .load(button_2_out), .Q(counter_1_q), .clk(or_1_out), .clr(comparator_1_gt));  // open: D, count, carry
  or or_1 (or_1_out, button_out, button_2_out);
  LED led_5 (.in(ON));
  LED led_6 (.in(ON));
  LED led_7 (.in(ON));
  LED led_8 (.in(ON));
  LED led_9 (.in(next_1_out_8));
  LED led_10 (.in(next_1_out_8));
  LED led_11 (.in(next_1_out_8));
  LED led_12 (.in(next_1_out_8));
  LED led_13 (.in(next_1_out_8));
  LED led_14 (.in(next_1_out_8));
  Comparator #(.width(6)) comparator_1 (.a(counter_1_q), .b(6'b000100), .gt(comparator_1_gt));  // open: eq, lt
  Hex_Digit_Display hex_digit_display_1 (.value(timer_1_out_5));  // open: dp
  DotMatrix dotmatrix_1 (
    .col0({7{1'b0}}), .col1(lettera_m_p_l_1_output), .col2(lettera_m_p_l_1_out_3),
    .col3(lettera_m_p_l_1_out_4), .col4({7{1'b0}}));
  lettera_M_P_L lettera_m_p_l_1 (
    .\output (lettera_m_p_l_1_output), .out_3(lettera_m_p_l_1_out_3), .out_4(lettera_m_p_l_1_out_4),
    .\input (next_1_out_6));
  next next_1 (
    .out_6(next_1_out_6), .out_8(next_1_out_8), .min1(min1), .min0(min0), .in_4(orario_1_out_3),
    .out_7(next_1_out_7), .in_5(ckl), .in_1(comparator_1_gt));
  orario orario_1 (.in_2(counter_1_q), .out_3(orario_1_out_3), .in_1(next_1_out_7));
  Hex_Digit_Display hex_digit_display_2 (.value(timer_1_out_6));  // open: dp
  DotMatrix dotmatrix_2 (
    .col0({7{1'b0}}), .col1(lettera_l_v_d_1_output), .col2(lettera_l_v_d_1_out_3),
    .col3(lettera_l_v_d_1_out_4), .col4({7{1'b0}}));
  DotMatrix dotmatrix_3 (
    .col0({7{1'b0}}), .col1(lettera_i_a_o_1_output), .col2(lettera_i_a_o_1_out_3),
    .col3(lettera_i_a_o_1_out_4), .col4({7{1'b0}}));
  lettera_L_V_D lettera_l_v_d_1 (
    .\output (lettera_l_v_d_1_output), .out_3(lettera_l_v_d_1_out_3), .out_4(lettera_l_v_d_1_out_4),
    .d(next_1_out_6));
  lettera__I_A_O lettera_i_a_o_1 (
    .\output (lettera_i_a_o_1_output), .out_3(lettera_i_a_o_1_out_3), .out_4(lettera_i_a_o_1_out_4),
    .o(next_1_out_6));
  Hex_Digit_Display hex_digit_display_3 (.value(min0));  // open: dp
  Hex_Digit_Display hex_digit_display_4 (.value(min1));  // open: dp
  timer timer_1 (
    .in_2(ON), .out_5(timer_1_out_5), .out_6(timer_1_out_6), .out_3(min1), .out_4(min0),
    .out_7(timer_1_out_7), .out_8(timer_1_out_8), .in_1(ckl));
  DotMatrix dotmatrix_4 (
    .col0({7{1'b0}}), .col1(lettera_a_i_i_1_output), .col2(lettera_a_i_i_1_out_3),
    .col3(lettera_a_i_i_1_out_4), .col4({7{1'b0}}));
  lettera_A__I__I lettera_a_i_i_1 (
    .\output (lettera_a_i_i_1_output), .out_3(lettera_a_i_i_1_out_3), .out_4(lettera_a_i_i_1_out_4),
    .i(next_1_out_6));
  DotMatrix dotmatrix_5 (
    .col0({7{1'b0}}), .col1(lettera_n_a_1_output), .col2(lettera_n_a_1_out_3), .col3(lettera_n_a_1_out_4),
    .col4({7{1'b0}}));
  DotMatrix dotmatrix_6 (
    .col0({7{1'b0}}), .col1(lettera_o_1_output), .col2(lettera_o_1_out_3), .col3(lettera_o_1_out_4),
    .col4({7{1'b0}}));
  lettera_O lettera_o_1 (
    .\output (lettera_o_1_output), .out_3(lettera_o_1_out_3), .out_4(lettera_o_1_out_4), .o(next_1_out_6));
  lettera_N_A lettera_n_a_1 (
    .\output (lettera_n_a_1_output), .out_3(lettera_n_a_1_out_3), .out_4(lettera_n_a_1_out_4),
    .\input (next_1_out_6));
  Hex_Digit_Display hex_digit_display_5 (.value(timer_1_out_7));  // open: dp
  Hex_Digit_Display hex_digit_display_6 (.value(timer_1_out_8));  // open: dp

  // Notes on the sheet:
  //   MILANO
  //   PAVIA
  //   LODI
  //   ORARIO
  //   5'  20'  35'  50'
  //   10'  25'  40'  55'
  //   15'  30'  45'  00'
  //   quando il circuito è spento anche il cartellone dovrebbe essere spento
  //   aumenta/abbassa ritardo
  //   RITARDO
  //   in ARRIVO
  //   ore
  //   TIMER
  //   minuti
  //   DESTINAZIONE
  //   secondi
endmodule

module lettera_M_P_L (
  input  [1:0] \input ,
  output [6:0] \output ,
  output [6:0] out_3,
  output [6:0] out_4
);

  Multiplexer #(.select(2), .width(7)) multiplexer_1 (
    .in0(7'b0111110), .in1(7'b0111110), .in2(7'b0111110), .out(\output ), .sel(\input ));  // open: in3, en
  Multiplexer #(.select(2), .width(7)) multiplexer_2 (
    .in0(7'b0010000), .in1(7'b0101000), .in2(7'b0000010), .out(out_3), .sel(\input ));  // open: in3, en
  Multiplexer #(.select(2), .width(7)) multiplexer_3 (
    .in0(7'b0111110), .in1(7'b0111000), .in2(7'b0000010), .out(out_4), .sel(\input ));  // open: in3, en

  // Notes on the sheet:
  //   m
  //   p
  //   l
  //   m
  //   p
  //   l
  //   m
  //   p
  //   l
endmodule

module lettera__I_A_O (
  input  [1:0] o,
  output [6:0] \output ,
  output [6:0] out_3,
  output [6:0] out_4
);

  Multiplexer #(.select(2), .width(7)) multiplexer_1 (
    .in0({7{1'b0}}), .in1(7'b0111110), .in2(7'b0111110), .out(\output ), .sel(o));  // open: in3, en
  Multiplexer #(.select(2), .width(7)) multiplexer_2 (
    .in0(7'b0111110), .in1(7'b0101000), .in2(7'b0100010), .out(out_3), .sel(o));  // open: in3, en
  Multiplexer #(.select(2), .width(7)) multiplexer_3 (
    .in0({7{1'b0}}), .in1(7'b0111110), .in2(7'b0111110), .out(out_4), .sel(o));  // open: in3, en

  // Notes on the sheet:
  //   input
  //   i
  //   a
  //   i
  //   a
  //   o
  //   i
  //   a
  //   o
endmodule

module lettera_L_V_D (
  input  [1:0] d,
  output [6:0] \output ,
  output [6:0] out_3,
  output [6:0] out_4
);

  Multiplexer #(.select(2), .width(7)) multiplexer_1 (
    .in0(7'b0111110), .in1(7'b0111100), .in2(7'b0111110), .out(\output ), .sel(d));  // open: in3, en
  Multiplexer #(.select(2), .width(7)) multiplexer_2 (
    .in0(7'b0000010), .in1(7'b0000010), .in2(7'b0100010), .out(out_3), .sel(d));  // open: in3, en
  Multiplexer #(.select(2), .width(7)) multiplexer_3 (
    .in0(7'b0000010), .in1(7'b0111100), .in2(7'b0011100), .out(out_4), .sel(d));  // open: in3, en

  // Notes on the sheet:
  //   l
  //   v
  //   input
  //   l
  //   v
  //   d
  //   l
  //   v
  //   d
endmodule

module lettera_A__I__I (
  input  [1:0] i,
  output [6:0] \output ,
  output [6:0] out_3,
  output [6:0] out_4
);

  Multiplexer #(.select(2), .width(7)) multiplexer_1 (
    .in0(7'b0111110), .in1({7{1'b0}}), .in2({7{1'b0}}), .out(\output ), .sel(i));  // open: in3, en
  Multiplexer #(.select(2), .width(7)) multiplexer_2 (
    .in0(7'b0101000), .in1(7'b0111110), .in2(7'b0111110), .out(out_3), .sel(i));  // open: in3, en
  Multiplexer #(.select(2), .width(7)) multiplexer_3 (
    .in0(7'b0111110), .in1({7{1'b0}}), .in2({7{1'b0}}), .out(out_4), .sel(i));  // open: in3, en

  // Notes on the sheet:
  //   input
  //   a
  //   i
  //   a
  //   i
  //   i
  //   a
  //   i
  //   i
endmodule

module lettera_N_A (
  input  [1:0] \input ,
  output [6:0] \output ,
  output [6:0] out_3,
  output [6:0] out_4
);

  Multiplexer #(.select(2), .width(7)) multiplexer_1 (
    .in0(7'b0111110), .in1(7'b0111110), .in2({7{1'b0}}), .out(\output ), .sel(\input ));  // open: in3, en
  Multiplexer #(.select(2), .width(7)) multiplexer_2 (
    .in0(7'b0100000), .in1(7'b0101000), .in2({7{1'b0}}), .out(out_3), .sel(\input ));  // open: in3, en
  Multiplexer #(.select(2), .width(7)) multiplexer_3 (
    .in0(7'b0011110), .in1(7'b0111110), .in2({7{1'b0}}), .out(out_4), .sel(\input ));  // open: in3, en

  // Notes on the sheet:
  //   n
  //   a
  //   n
  //   a
  //   n
  //   a
endmodule

module lettera_O (
  input  [1:0] o,
  output [6:0] \output ,
  output [6:0] out_3,
  output [6:0] out_4
);

  Multiplexer #(.select(2), .width(7)) multiplexer_1 (
    .in0(7'b0111110), .in1({7{1'b0}}), .in2({7{1'b0}}), .out(\output ), .sel(o));  // open: in3, en
  Multiplexer #(.select(2), .width(7)) multiplexer_2 (
    .in0(7'b0100010), .in1({7{1'b0}}), .in2({7{1'b0}}), .out(out_3), .sel(o));  // open: in3, en
  Multiplexer #(.select(2), .width(7)) multiplexer_3 (
    .in0(7'b0111110), .in1({7{1'b0}}), .in2({7{1'b0}}), .out(out_4), .sel(o));  // open: in3, en

  // Notes on the sheet:
  //   input
  //   o
  //   o
endmodule

module next (
  input  in_1,
  input  [3:0] min1,
  input  [3:0] min0,
  input  [5:0] in_4,
  input  in_5,
  output [1:0] out_6,
  output [3:0] out_7,
  output out_8
);

  wire comparator_1_eq, comparator_2_lt, or_1_out;
  wire [5:0] adder_1_out, bit_extender_1_out, bit_extender_2_out, multiplier_1_out, subtractor_1_out;

  assign bit_extender_1_out = {{2{1'b0}}, min1};  // Bit_Extender bit_extender_1
  assign bit_extender_2_out = {{2{1'b0}}, min0};  // Bit_Extender bit_extender_2
  Multiplier #(.width(6)) multiplier_1 (
    .a(bit_extender_1_out), .b(6'b001010), .out(multiplier_1_out));  // open: cin, cout
  Adder #(.width(6)) adder_1 (.a(multiplier_1_out), .b(bit_extender_2_out), .out(adder_1_out));  // open: cin, cout
  Subtractor #(.width(6)) subtractor_1 (.a(in_4), .b(6'b000010), .out(subtractor_1_out));  // open: bin, bout
  Comparator #(.width(6)) comparator_1 (.a(adder_1_out), .b(in_4), .eq(comparator_1_eq));  // open: gt, lt
  Comparator #(.width(6)) comparator_2 (.a(subtractor_1_out), .b(adder_1_out), .lt(comparator_2_lt));  // open: gt, eq
  or or_1 (or_1_out, in_1, comparator_1_eq);
  and and_1 (out_8, comparator_2_lt, in_5);
  Counter #(.width(2), .max('h2)) counter_1 (.Q(out_6), .clk(or_1_out));  // open: load, D, count, carry, clr
  Counter #(.width(4), .max('hb)) counter_2 (.Q(out_7), .clk(or_1_out));  // open: load, D, count, carry, clr

  // Notes on the sheet:
  //   inputa da orario
  //   input da orario
  //   se la somma dell'orario coincide esco 
  //   output per orario
  //   stazione successiva
  //   quando macano 2 min accendo i led
endmodule

module timer (
  input  in_1,
  input  in_2,
  output [3:0] out_3,
  output [3:0] out_4,
  output [3:0] out_5,
  output [3:0] out_6,
  output [3:0] out_7,
  output [3:0] out_8
);

  wire J, not_1_out, P, x, Y, Z;

  Counter #(.width(4), .max('h5), .trigger("falling")) counter_1 (
    .Q(out_5), .clk(P), .clr(not_1_out));  // open: load, D, count, carry
  not not_1 (not_1_out, in_2);
  Counter #(.width(4), .max('h9), .trigger("falling")) counter_2 (
    .Q(out_6), .carry(P), .clk(J), .clr(not_1_out));  // open: load, D, count
  Counter #(.width(4), .max('h5), .trigger("falling")) counter_3 (
    .Q(out_3), .carry(J), .clk(Z), .clr(not_1_out));  // open: load, D, count
  Counter #(.width(4), .max('h9), .trigger("falling")) counter_4 (
    .Q(out_4), .carry(Z), .clk(Y), .clr(not_1_out));  // open: load, D, count
  Counter #(.width(4), .max('h9), .trigger("falling")) counter_5 (
    .Q(out_8), .carry(x), .clk(in_1), .clr(not_1_out));  // open: load, D, count
  Counter #(.width(4), .max('h5), .trigger("falling")) counter_6 (
    .Q(out_7), .carry(Y), .clk(x), .clr(not_1_out));  // open: load, D, count

  // Notes on the sheet:
  //   ore
  //   minuti
  //   secondi
endmodule

module orario (
  input  [3:0] in_1,
  input  [5:0] in_2,
  output [5:0] out_3
);

  wire [5:0] rom_1_data;

  ROM #(.addrWidth(4), .dataWidth(6)) rom_1 (.addr(in_1), .data(rom_1_data));  // open: sel
  Adder #(.width(6)) adder_1 (.a(rom_1_data), .b(in_2), .out(out_3));  // open: cin, cout

  // Notes on the sheet:
  //   voglio che ogni 5 minuti cambi stazione
  //   contents of rom_1 (hex, n*v repeats v):
  //   5 a f 14 19 1e 23 28 2d 32 37
  //   - quando funtiona divetera un input 
  //   adder per il ritardo
endmodule
